// Logisim project dhad_cpu.circ as structural Verilog: 24 circuits, main circuit CPU
module NAND2 (
  input  [7:0] A_7_0,
  input  [7:0] B_7_0,
  output [7:0] Q_7_0
);

  // NAND_Gate nand_1 has open pins: out=Q_7_0
endmodule

module NOT1 (
  input  [7:0] A_7_0,
  output [7:0] Q_7_0
);

  // NOT_Gate not_1 has open pins: in=open, out=Q_7_0
endmodule

module AND2 (
  input  [7:0] A_7_0,
  input  [7:0] B_7_0,
  output [7:0] Q_7_0
);

  // AND_Gate and_1 has open pins: out=Q_7_0
endmodule

module OR2 (
  input  [7:0] A_7_0,
  input  [7:0] B_7_0,
  output [7:0] Q_7_0
);

  // OR_Gate or_1 has open pins: out=Q_7_0
endmodule

module XOR2 (
  input  [7:0] A_7_0,
  input  [7:0] B_7_0,
  output [7:0] Q_7_0
);

  // XOR_Gate xor_1 has open pins: out=Q_7_0
endmodule

module MUX2_1 (
  input  [7:0] A_7_0,
  input  [7:0] B_7_0,
  input  Sel,
  output [7:0] Q_7_0
);

  Multiplexer #(.select(1), .width(8)) multiplexer_1 (.out(Q_7_0));  // open: in0, in1, sel, en
endmodule

module MUX8_1 (
  input  [7:0] I0_7_0,
  input  [7:0] I1_7_0,
  input  [7:0] I2_7_0,
  input  [7:0] I3_7_0,
  input  [7:0] I4_7_0,
  input  [7:0] I5_7_0,
  input  [7:0] I6_7_0,
  input  [7:0] I7_7_0,
  input  [2:0] Sel_2_0,
  output [7:0] Q_7_0
);

  wire [7:0] M0_out, M1_out, M2_out, M3_out, M4_out, M5_out;

  Multiplexer #(.select(1), .width(8)) M0 (.out(M0_out));  // open: in0, in1, sel, en
  Multiplexer #(.select(1), .width(8)) M1 (.out(M1_out));  // open: in0, in1, sel, en
  Multiplexer #(.select(1), .width(8)) M2 (.out(M2_out));  // open: in0, in1, sel, en
  Multiplexer #(.select(1), .width(8)) M3 (.out(M3_out));  // open: in0, in1, sel, en
  Multiplexer #(.select(1), .width(8)) M4 (.out(M4_out));  // open: in0, in1, sel, en
  Multiplexer #(.select(1), .width(8)) M5 (.out(M5_out));  // open: in0, in1, sel, en
  Multiplexer #(.select(1), .width(8)) M6 (.out(Q_7_0));  // open: in0, in1, sel, en
endmodule

module DECODER_3to8 (
  input  [2:0] Sel_2_0,
  output Y0,
  output Y1,
  output Y2,
  output Y3,
  output Y4,
  output Y5,
  output Y6,
  output Y7
);

  // Decoder #(.select(3)) decoder_1: pin names not known; wires that end beside it: Sel_2_0, Y0, Y1, Y2, Y3, Y4, Y5, Y6
endmodule

module HALF_ADDER (
  input  A,
  input  B,
  output Sum,
  output Carry
);

  // XOR_Gate XOR has open pins: out=Sum
  // AND_Gate AND: pin names not known; wires that end beside it: A, B, Carry
endmodule

module FULL_ADDER (
  input  A,
  input  B,
  input  Cin,
  output Sum,
  output Cout
);

  wire HA1_p1, HA1_p2, HA2_p1;

  // HALF_ADDER HA1: pin names not known; wires that end beside it: HA1_p1, HA1_p2
  // HALF_ADDER HA2: pin names not known; wires that end beside it: HA2_p1, HA1_p2
  // OR_Gate OR: pin names not known; wires that end beside it: HA1_p2, HA1_p2, Cout
endmodule

module ADDER_8 (
  input  [7:0] A_7_0,
  input  [7:0] B_7_0,
  input  Cin,
  output [7:0] Sum_7_0,
  output Cout
);

  wire FA0_p1, FA0_p3, FA1_p3, FA2_p3, FA3_p3, FA4_p3, FA5_p3, FA6_p3;

  // FULL_ADDER FA0: pin names not known; wires that end beside it: FA0_p1, Cin, FA0_p3
  // FULL_ADDER FA1: pin names not known; wires that end beside it: FA0_p3, Cin, FA1_p3
  // FULL_ADDER FA2: pin names not known; wires that end beside it: FA1_p3, Cin, FA2_p3
  // FULL_ADDER FA3: pin names not known; wires that end beside it: FA2_p3, Cin, FA3_p3
  // FULL_ADDER FA4: pin names not known; wires that end beside it: FA3_p3, Cin, FA4_p3
  // FULL_ADDER FA5: pin names not known; wires that end beside it: FA4_p3, Cin, FA5_p3
  // FULL_ADDER FA6: pin names not known; wires that end beside it: FA5_p3, Cin, FA6_p3
  // FULL_ADDER FA7: pin names not known; wires that end beside it: FA6_p3, Cout
  // Pins of 2 and 8 bits meet at A_7_0
  // Pins of 2 and 8 bits meet at B_7_0
endmodule

module SUBTRACTOR_8 (
  input  [7:0] A_7_0,
  input  [7:0] B_7_0,
  output [7:0] Diff_7_0,
  output Bout
);

  wire xor_1_p3;

  // XOR_Gate #(.width(8)) xor_1: pin names not known; wires that end beside it: A_7_0, A_7_0, xor_1_p3
  // ADDER_8 ADD: pin names not known; wires that end beside it: Diff_7_0, Bout

  assign B_7_0 = A_7_0;
endmodule

module ALU_8 (
  input  [7:0] A_7_0,
  input  [7:0] B_7_0,
  input  [3:0] ALU_OP_3_0,
  output [7:0] RESULT_7_0,
  output Z,
  output N,
  output C
);

  wire NAND_OP_p3, XOR_OP_p4;
  wire [7:0] AND_OP_out, NOT_OP_out, OR_OP_out;

  assign AND_OP_out = A_7_0 & B_7_0;  // AND_Gate AND_OP, 8 bits wide
  assign OR_OP_out = A_7_0 | B_7_0;  // OR_Gate OR_OP, 8 bits wide
  // XOR_Gate #(.width(8)) XOR_OP: pin names not known; wires that end beside it: B_7_0, A_7_0, B_7_0, XOR_OP_p4
  // NOT_Gate NOT_OP has open pins: in=open, out=NOT_OP_out
  // NAND_Gate #(.width(8)) NAND_OP: pin names not known; wires that end beside it: A_7_0, B_7_0, NAND_OP_p3
  Multiplexer #(.select(3), .width(8)) RESULT_MUX ();  // open: in0, in1, in2, in3, in4, in5, in6, in7, out, sel, en
endmodule

module REGISTER_8 (
  input  [7:0] D_7_0,
  input  WE,
  input  CLK,
  input  RST,
  output [7:0] Q_7_0
);

  Register #(.width(8)) register_1 (.Q(Q_7_0));  // open: D, en, clk, clr
  // also tied to GND on the sheet: RST
endmodule

module REGISTER_FILE_8x8 (
  input  [2:0] RdAddr1_2_0,
  input  [2:0] RdAddr2_2_0,
  input  [2:0] WrAddr_2_0,
  input  [7:0] WrData_7_0,
  input  WE,
  input  CLK,
  output [7:0] RdData1_7_0,
  output [7:0] RdData2_7_0
);

  wire S1_p1, S1_p2, S2_p1, S2_p2, S3_p1, S3_p2, S4_p1, S4_p2, S5_p1, S5_p2, S6_p1, S6_p2, S7_p1, S7_p2,
       WR_DEC_p1, WR_DEC_p2, WR_DEC_p3, WR_DEC_p4, WR_DEC_p5, WR_DEC_p6, WR_DEC_p7;

  // DECODER_3to8 WR_DEC: pin names not known; wires that end beside it: WR_DEC_p1, WR_DEC_p2, WR_DEC_p3, WR_DEC_p4, WR_DEC_p5, WR_DEC_p6, WR_DEC_p7
  REGISTER_8 S0 ();  // open: D_7_0, WE, CLK, RST, Q_7_0
  // REGISTER_8 S1: pin names not known; wires that end beside it: S1_p1, S1_p2
  // REGISTER_8 S2: pin names not known; wires that end beside it: S2_p1, S2_p2
  // REGISTER_8 S3: pin names not known; wires that end beside it: S3_p1, S3_p2
  // REGISTER_8 S4: pin names not known; wires that end beside it: S4_p1, S4_p2
  // REGISTER_8 S5: pin names not known; wires that end beside it: S5_p1, S5_p2
  // REGISTER_8 S6: pin names not known; wires that end beside it: S6_p1, S6_p2
  // REGISTER_8 S7: pin names not known; wires that end beside it: S7_p1, S7_p2
  // Multiplexer #(.select(3), .width(8)) RD_MUX1: pin names not known; wires that end beside it: {RdData1_7_0[7:3], RdAddr1_2_0}
  Multiplexer #(.select(3), .width(8)) RD_MUX2 (.out(RdData2_7_0));  // open: in0, in1, in2, in3, in4, in5, in6, in7, sel, en
  // Pins of 3 and 8 bits meet at {RdData1_7_0[7:3], RdAddr1_2_0}

  assign RdData1_7_0[2:0] = RdAddr1_2_0;
endmodule

module ACC_8 (
  input  [7:0] D_7_0,
  input  WE,
  input  CLK,
  input  RST,
  output [7:0] Q_7_0
);

  Register #(.width(8)) ACC (.Q(Q_7_0));  // open: D, en, clk, clr
  // also tied to GND on the sheet: RST
endmodule

module FLAGS_REG (
  input  [7:0] D_7_0,
  input  WE,
  input  CLK,
  input  RST,
  output Z,
  output N,
  output C
);

  wire [7:0] FLAGS_q;

  Register #(.width(8)) FLAGS (.Q(FLAGS_q));  // open: D, en, clk, clr
  // Bit_Selector #(.lower(0), .upper(0), .width(8)) bit_selector_1: pin names not known; wires that end beside it: Z
  // Bit_Selector #(.lower(1), .upper(1), .width(8)) bit_selector_2: pin names not known; wires that end beside it: CLK, N
  // Bit_Selector #(.lower(2), .upper(2), .width(8)) bit_selector_3: pin names not known; wires that end beside it: FLAGS_q, C
  // also tied to GND on the sheet: RST
endmodule

module PC_16 (
  input  [15:0] D_15_0,
  input  WE,
  input  CLK,
  input  HALT,
  output [15:0] Q_15_0
);

  Register #(.width(16)) PC (.Q(Q_15_0));  // open: D, en, clk, clr
endmodule

module SP_8 (
  input  [7:0] D_7_0,
  input  WE,
  input  CLK,
  input  RST,
  output [7:0] Q_7_0
);

  Register #(.width(8)) SP (.Q(Q_7_0));  // open: D, en, clk, clr
  // also tied to GND on the sheet: RST
endmodule

module INSTRUCTION_REGISTER (
  input  [7:0] D_7_0,
  input  IR_LOAD,
  input  CLK,
  output [3:0] OPCODE_3_0,
  output [3:0] REG_3_0
);

  wire [7:0] IR_REG_q;

  Register #(.width(8)) IR_REG (.Q(IR_REG_q));  // open: D, en, clk, clr
  // Bit_Selector #(.lower(4), .upper(7), .width(8)) OPCODE_BS: pin names not known; wires that end beside it: OPCODE_3_0
  // Bit_Selector #(.lower(0), .upper(3), .width(8)) REG_BS: pin names not known; wires that end beside it: CLK, IR_REG_q, REG_3_0
endmodule

module RAM_64K (
  input  [15:0] ADDR_15_0,
  input  [7:0] WDATA_7_0,
  input  WE,
  input  CLK,
  output [7:0] RDATA_7_0
);

  // RAM #(.addr_bits(16), .data_bits(8)) ram_1: pin names not known; wires that end beside it: WDATA_7_0, WE, RDATA_7_0
endmodule

module CONTROL_UNIT (
  input  [3:0] OPCODE_3_0,
  input  [3:0] EXT_OP_3_0,
  input  CLK,
  input  RST,
  input  Z_FLAG,
  input  N_FLAG,
  input  C_FLAG,
  output IR_LOAD,
  output PC_INC,
  output PC_LOAD,
  output MEM_READ,
  output MEM_WRITE,
  output ACC_WRITE,
  output REG_WRITE,
  output FLAGS_WRITE,
  output [3:0] ALU_OP,
  output [1:0] ALU_A_SRC,
  output [1:0] ALU_B_SRC,
  output [1:0] WR_SRC,
  output [1:0] MEM_ADDR_SRC,
  output SP_INC,
  output SP_DEC,
  output HALT
);


  assign ACC_WRITE = 1'b0;
  assign ALU_A_SRC = 2'b00;
  assign ALU_B_SRC = 2'b00;
  assign ALU_OP = 4'b0000;
  assign FLAGS_WRITE = 1'b0;
  assign HALT = 1'b0;
  assign IR_LOAD = 1'b0;
  assign MEM_ADDR_SRC = 2'b00;
  assign MEM_READ = 1'b0;
  assign MEM_WRITE = 1'b0;
  assign PC_INC = 1'b0;
  assign PC_LOAD = 1'b0;
  assign REG_WRITE = 1'b0;
  assign SP_DEC = 1'b0;
  assign SP_INC = 1'b0;
  assign WR_SRC = 2'b00;
endmodule

module DATAPATH (
  input  CLK,
  input  RST,
  input  [7:0] MEM_RDATA_7_0,
  input  IR_LOAD,
  input  PC_INC,
  input  PC_LOAD,
  input  MEM_READ,
  input  MEM_WRITE,
  input  ACC_WRITE,
  input  REG_WRITE,
  input  FLAGS_WRITE,
  input  [3:0] ALU_OP_3_0,
  input  [1:0] ALU_A_SRC_1_0,
  input  [1:0] ALU_B_SRC_1_0,
  input  [1:0] WR_SRC_1_0,
  input  [1:0] MEM_ADDR_SRC_1_0,
  input  SP_INC,
  input  SP_DEC,
  output [15:0] MEM_ADDR_15_0,
  output [7:0] MEM_WDATA_7_0,
  output [3:0] OPCODE_3_0,
  output [3:0] REG_3_0,
  output Z_FLAG,
  output N_FLAG,
  output C_FLAG,
  output [7:0] ACC_OUT_7_0,
  output [15:0] PC_OUT_15_0
);

  PC_16 PC ();  // open: D_15_0, WE, CLK, HALT, Q_15_0
  SP_8 SP ();  // open: D_7_0, WE, CLK, RST, Q_7_0
  // INSTRUCTION_REGISTER IR: pin names not known; wires that end beside it: OPCODE_3_0, REG_3_0
  // ACC_8 ACC: pin names not known; wires that end beside it: ACC_OUT_7_0
  REGISTER_FILE_8x8 REG_FILE ();  // open: RdAddr1_2_0, RdAddr2_2_0, WrAddr_2_0, WrData_7_0, WE, CLK, RdData1_7_0, RdData2_7_0
  ALU_8 ALU ();  // open: A_7_0, B_7_0, ALU_OP_3_0, RESULT_7_0, Z, N, C
  // FLAGS_REG FLAGS: pin names not known; wires that end beside it: Z_FLAG, N_FLAG, C_FLAG

  assign PC_OUT_15_0 = MEM_ADDR_15_0;
endmodule

module CPU (
  input  CLK,
  input  RST,
  output [7:0] ACC_7_0,
  output [15:0] PC_15_0,
  output HALTED
);

  RAM_64K RAM ();  // open: ADDR_15_0, WDATA_7_0, WE, CLK, RDATA_7_0
  DATAPATH DP ();  // open: CLK, RST, MEM_RDATA_7_0, IR_LOAD, PC_INC, PC_LOAD, MEM_READ, MEM_WRITE, ACC_WRITE, REG_WRITE, FLAGS_WRITE, ALU_OP_3_0, ALU_A_SRC_1_0, ALU_B_SRC_1_0, WR_SRC_1_0, MEM_ADDR_SRC_1_0, SP_INC, SP_DEC, MEM_ADDR_15_0, MEM_WDATA_7_0, OPCODE_3_0, REG_3_0, Z_FLAG, N_FLAG, C_FLAG, ACC_OUT_7_0, PC_OUT_15_0
  CONTROL_UNIT CTRL ();  // open: OPCODE_3_0, EXT_OP_3_0, CLK, RST, Z_FLAG, N_FLAG, C_FLAG, IR_LOAD, PC_INC, PC_LOAD, MEM_READ, MEM_WRITE, ACC_WRITE, REG_WRITE, FLAGS_WRITE, ALU_OP, ALU_A_SRC, ALU_B_SRC, WR_SRC, MEM_ADDR_SRC, SP_INC, SP_DEC, HALT
  // Pins of 8 and 16 bits meet at {PC_15_0[15:8], ACC_7_0}

  assign PC_15_0[7:0] = ACC_7_0;
endmodule
